# Fritzing sketch proxygambit (saved by Fritzing 0.9.2b)
breadboards: 1

parts:
  Part1 = Arduino Nano (Rev3.0)
  Part2 = Adafruit FONA - Mini Cellular GSM Breakout
  Raspberry_Pi1 = Raspberry Pi 2
  R1 = Resistor [tolerance=±5% resistance=1.6k package=THT]
  R2 = Resistor [tolerance=±5% resistance=3.3k package=THT]

nets:
  N1: Part1.D1/TX, R1.Pin_1, R2.Pin_0
  N2: Part1.D0/RX, Raspberry_Pi1.GPIO14
  GND: Part1.GND, Part2.PWRKEY_5V, Part2.GND, Raspberry_Pi1.GND, R2.Pin_1
  N3: Part1.D2, Part2.RXD_5V
  N4: Part1.D3, Part2.TXD_5V
  N5: Part1.D4, Part2.RESET_5V
  5V: Part1.5V, Part2.VCCIO, Part2.+5V, Raspberry_Pi1.5V
  N6: Raspberry_Pi1.GPIO15, R1.Pin_0

custom parts:
  Adafruit FONA - Mini Cellular GSM Breakout: An all-in-one cellular phone module that lets you add voice, text, SMS and GPRS data to your project. Quad-band 850/900/1800/1900MHz - connect onto any global GSM network with any 2G SIM. Includes an onboard LiPoly battery charging circuitry so you can take your project on the go. Also works as an FM radio receiver.
